// Logisim project my_adder.circ as structural Verilog: 3 circuits, main circuit main
module main (
  input  [15:0] A,
  input  [15:0] B,
  input  sub,
  output [15:0] result,
  output ovf
);

  wire adder1_1_cout1, adder5_1_cout5, adder5_2_cout5, adder5_3_cout5, B_3;
  wire [4:0] B_0, B_1, B_2;

  adder5 adder5_1 (.Cin5(sub), .a5(A[4:0]), .b5(B_0), .sum5(result[4:0]), .Cout5(adder5_1_cout5));
  adder5 adder5_2 (.Cin5(adder5_1_cout5), .a5(A[9:5]), .b5(B_1), .sum5(result[9:5]), .Cout5(adder5_2_cout5));
  adder5 adder5_3 (.Cin5(adder5_2_cout5), .a5(A[14:10]), .b5(B_2), .sum5(result[14:10]), .Cout5(adder5_3_cout5));
  xor xor_1 (B_3, sub, B[15]);
  assign B_2 = {5{sub}} ^ B[14:10];  // XOR_Gate xor_2, 5 bits wide
  assign B_1 = {5{sub}} ^ B[9:5];  // XOR_Gate xor_3, 5 bits wide
  assign B_0 = {5{sub}} ^ B[4:0];  // XOR_Gate xor_4, 5 bits wide
  adder1 adder1_1 (.Cin1(adder5_3_cout5), .a1(A[15]), .b1(B_3), .sum1(result[15]), .Cout1(adder1_1_cout1));
  xor xor_5 (ovf, adder5_3_cout5, adder1_1_cout1);

  // Other names for the same wires on the sheet: sub_tun = sub; A_0[4:0] = A[4:0]; A_1[4:0] = A[9:5];
  //   A_2[4:0] = A[14:10]; A_3 = A[15]; B_0s[4:0] = B[4:0]; B_1s[4:0] = B[9:5]; B_2s[4:0] = B[14:10]; B_3s = B[15];
  //   result_0[4:0] = result[4:0]; result_1[4:0] = result[9:5]; result_2[4:0] = result[14:10]; result_3 = result[15]
endmodule

module adder1 (
  input  Cin1,
  input  a1,
  input  b1,
  output sum1,
  output Cout1
);

  wire and_1_out, and_2_out, xor_1_out;

  and and_1 (and_1_out, b1, a1);
  xor xor_1 (xor_1_out, a1, b1);
  or or_1 (Cout1, and_1_out, and_2_out);
  and and_2 (and_2_out, xor_1_out, Cin1);
  xor xor_2 (sum1, Cin1, xor_1_out);
endmodule

module adder5 (
  input  Cin5,
  input  [4:0] a5,
  input  [4:0] b5,
  output [4:0] sum5,
  output Cout5
);

  wire adder1_1_cout1, adder1_2_cout1, adder1_3_cout1, adder1_4_cout1;

  adder1 adder1_1 (.Cin1(Cin5), .a1(a5[0]), .b1(b5[0]), .sum1(sum5[0]), .Cout1(adder1_1_cout1));
  adder1 adder1_2 (.Cin1(adder1_1_cout1), .a1(a5[1]), .b1(b5[1]), .sum1(sum5[1]), .Cout1(adder1_2_cout1));
  adder1 adder1_3 (.Cin1(adder1_2_cout1), .a1(a5[2]), .b1(b5[2]), .sum1(sum5[2]), .Cout1(adder1_3_cout1));
  adder1 adder1_4 (.Cin1(adder1_3_cout1), .a1(a5[3]), .b1(b5[3]), .sum1(sum5[3]), .Cout1(adder1_4_cout1));
  adder1 adder1_5 (.Cin1(adder1_4_cout1), .a1(a5[4]), .b1(b5[4]), .sum1(sum5[4]), .Cout1(Cout5));

  // Other names for the same wires on the sheet: a5_0 = a5[0]; a5_1 = a5[1]; a5_2 = a5[2]; a5_3 = a5[3]; a5_4 = a5[4];
  //   b5_0 = b5[0]; b5_1 = b5[1]; b5_2 = b5[2]; b5_3 = b5[3]; b5_4 = b5[4]; sum5_0 = sum5[0]; sum5_1 = sum5[1];
  //   sum5_2 = sum5[2]; sum5_3 = sum5[3]; sum5_4 = sum5[4]
endmodule
