// Logisim project vending.circ as structural Verilog: 7 circuits, main circuit main
module main (
  input  N,
  input  D,
  input  RESET,
  output DISPENSE,
  output DESPERATE,
  output DOH
);

  wire clk, D0, D1, D2, In1, In2, Q0, Q1, Q2;
  wire [1:0] multiplexer_1_out, multiplexer_2_out;

  Clock clock_1 (.out(clk));
  D_Flip_Flop d_ff_1 (.D(D0), .clk(clk), .Q(Q0));  // open: Qn, preset, reset
  D_Flip_Flop d_ff_2 (.D(D1), .clk(clk), .Q(Q1));  // open: Qn, preset, reset
  D_Flip_Flop d_ff_3 (.D(D2), .clk(clk), .Q(Q2));  // open: Qn, preset, reset
  D0_logic d0_logic_1 (.Q0(Q0), .Q1(Q1), .Q2(Q2), .In1(In1), .In2(In2), .D0(D0));
  D1_logic d1_logic_1 (.in_1(Q0), .in_2(Q1), .in_3(Q2), .in_4(In1), .in_5(In2), .D1(D1));
  D2_logic d2_logic_1 (.in_1(Q0), .in_2(Q1), .in_3(Q2), .in_4(In1), .in_5(In2), .D2(D2));
  DOH_logic doh_logic_1 (.in_1(Q0), .in_2(Q1), .in_3(Q2), .DOH(DOH));
  DESPERATE_logic desperate_logic_1 (.in_1(Q0), .in_2(Q1), .in_3(Q2), .DESPERATE(DESPERATE));
  DISPENSE_logic dispense_logic_1 (.in_1(Q0), .in_2(Q1), .in_3(Q2), .out_4(DISPENSE));
  Multiplexer #(.select(3), .width(2), .enable("false")) multiplexer_1 (
    .in0(2'b00), .in1(2'b01), .in2(2'b10), .in4(2'b11), .in5(2'b01), .in6(2'b10), .out(multiplexer_1_out),
    .sel({RESET, D, N}));  // open: in3, in7
  Multiplexer #(.select(3), .width(2), .enable("false")) multiplexer_2 (
    .in0(2'b00), .in1(2'b01), .in2(2'b10), .in4(2'b11), .in5(2'b11), .in6(2'b11), .out(multiplexer_2_out),
    .sel({RESET, D, N}));  // open: in3, in7
  Multiplexer #(.width(2), .enable("false")) multiplexer_3 (
    .in0(multiplexer_1_out), .in1(multiplexer_2_out), .out({In1, In2}), .sel(DISPENSE));

  // Other names for the same wires on the sheet: N_t = N; D_t = D; RESET_t = RESET; DESPERATE_t = DESPERATE;
  //   DISPENSE_t = DISPENSE; DOH_t = DOH

  // Notes on the sheet:
  //   s0
  //   s1
  //   s2
endmodule

module D0_logic (
  input  Q0,
  input  Q1,
  input  Q2,
  input  In1,
  input  In2,
  output D0
);

  wire and1, and2, and3, and4, and5, and6, and7, and8, and9, and10, and11, and12, and13, and14, not_1_out,
       not_2_out, not_3_out, not_4_out, not_5_out, not_6_out, not_7_out, not_8_out, not_9_out, not_10_out,
       not_11_out, not_12_out, not_13_out, not_14_out, not_15_out, not_16_out, not_17_out, not_18_out,
       not_19_out, not_20_out, not_21_out, not_22_out, not_23_out, not_24_out, not_25_out, not_26_out,
       not_27_out, not_28_out, not_29_out, not_30_out, not_31_out, not_32_out, not_33_out, not_34_out,
       not_35_out, not_36_out, not_37_out;

  not not_1 (not_1_out, Q0);
  not not_2 (not_2_out, Q1);
  not not_3 (not_3_out, In2);
  not not_4 (not_4_out, Q0);
  not not_5 (not_5_out, Q2);
  not not_6 (not_6_out, In1);
  not not_7 (not_7_out, Q0);
  not not_8 (not_8_out, Q2);
  not not_9 (not_9_out, In2);
  not not_10 (not_10_out, Q2);
  not not_11 (not_11_out, In1);
  and and_1 (and1, not_1_out, not_2_out, Q2, In1, not_3_out);
  and and_2 (and2, not_4_out, Q1, not_5_out, not_6_out, In2);
  and and_3 (and3, not_7_out, Q1, not_8_out, In1, not_9_out);
  and and_4 (and13, Q0, Q1, not_10_out, not_11_out, In2);
  not not_12 (not_12_out, Q0);
  not not_13 (not_13_out, In1);
  not not_14 (not_14_out, Q0);
  not not_15 (not_15_out, In2);
  not not_16 (not_16_out, Q1);
  not not_17 (not_17_out, Q2);
  not not_18 (not_18_out, In1);
  not not_19 (not_19_out, In2);
  not not_20 (not_20_out, Q2);
  not not_21 (not_21_out, In2);
  and and_5 (and4, not_12_out, Q1, Q2, not_13_out, In2);
  and and_6 (and5, not_14_out, Q1, Q2, In1, not_15_out);
  and and_7 (and6, Q0, not_16_out, not_17_out, not_18_out, not_19_out);
  and and_8 (and14, Q0, Q1, not_20_out, In1, not_21_out);
  not not_22 (not_22_out, Q1);
  not not_23 (not_23_out, Q2);
  not not_24 (not_24_out, In1);
  not not_25 (not_25_out, Q1);
  not not_26 (not_26_out, Q2);
  not not_27 (not_27_out, In2);
  not not_28 (not_28_out, Q1);
  not not_29 (not_29_out, In1);
  not not_30 (not_30_out, In2);
  or or_1 (D0, and1, and2, and3, and4, and5, and6, and7, and8, and9, and10, and11, and12, and13, and14);
  and and_9 (and7, Q0, not_22_out, not_23_out, not_24_out, In2);
  and and_10 (and8, Q0, not_25_out, not_26_out, In1, not_27_out);
  and and_11 (and9, Q0, not_28_out, Q2, not_29_out, not_30_out);
  not not_31 (not_31_out, Q1);
  not not_32 (not_32_out, In1);
  not not_33 (not_33_out, Q1);
  not not_34 (not_34_out, In2);
  not not_35 (not_35_out, Q2);
  not not_36 (not_36_out, In1);
  not not_37 (not_37_out, In2);
  and and_12 (and10, Q0, not_31_out, Q2, not_32_out, In2);
  and and_13 (and11, Q0, not_33_out, Q2, In1, not_34_out);
  and and_14 (and12, Q0, Q1, not_35_out, not_36_out, not_37_out);

  // Other names for the same wires on the sheet: In1_t = In1; In2_t = In2; Q0_t = Q0; Q1_t = Q1; Q2_t = Q2
endmodule

module D1_logic (
  input  in_1,
  input  in_2,
  input  in_3,
  input  in_4,
  input  in_5,
  output D1
);

  wire and1, and2, and3, and4, and5, and6, and7, and8, and9, and10, not_1_out, not_2_out, not_3_out,
       not_4_out, not_5_out, not_6_out, not_7_out, not_8_out, not_9_out, not_10_out, not_11_out, not_12_out,
       not_13_out, not_14_out, not_15_out, not_16_out, not_17_out, not_18_out, not_19_out, not_20_out,
       not_21_out, not_22_out, not_23_out, not_24_out, not_25_out, not_26_out, not_27_out;

  not not_1 (not_1_out, in_1);
  not not_2 (not_2_out, in_2);
  not not_3 (not_3_out, in_3);
  not not_4 (not_4_out, in_5);
  not not_5 (not_5_out, in_1);
  not not_6 (not_6_out, in_2);
  not not_7 (not_7_out, in_4);
  not not_8 (not_8_out, in_1);
  not not_9 (not_9_out, in_3);
  not not_10 (not_10_out, in_4);
  not not_11 (not_11_out, in_5);
  and and_1 (and1, not_1_out, not_2_out, not_3_out, in_4, not_4_out);
  and and_2 (and2, not_5_out, not_6_out, in_3, not_7_out, in_5);
  and and_3 (and3, not_8_out, in_2, not_9_out, not_10_out, not_11_out);
  not not_12 (not_12_out, in_1);
  not not_13 (not_13_out, in_3);
  not not_14 (not_14_out, in_5);
  not not_15 (not_15_out, in_1);
  not not_16 (not_16_out, in_3);
  not not_17 (not_17_out, in_1);
  not not_18 (not_18_out, in_4);
  not not_19 (not_19_out, in_5);
  and and_4 (and4, not_12_out, in_2, not_13_out, in_4, not_14_out);
  and and_5 (and5, not_15_out, in_2, not_16_out, in_4, in_5);
  and and_6 (and6, not_17_out, in_2, in_3, not_18_out, not_19_out);
  not not_20 (not_20_out, in_1);
  not not_21 (not_21_out, in_3);
  not not_22 (not_22_out, in_4);
  not not_23 (not_23_out, in_5);
  not not_24 (not_24_out, in_3);
  not not_25 (not_25_out, in_4);
  and and_7 (and7, not_20_out, in_2, in_3, in_4, in_5);
  and and_8 (and8, in_1, in_2, not_21_out, not_22_out, not_23_out);
  and and_9 (and9, in_1, in_2, not_24_out, not_25_out, in_5);
  or or_1 (D1, and1, and2, and3, and4, and5, and6, and7, and8, and9, and10);
  not not_26 (not_26_out, in_3);
  not not_27 (not_27_out, in_5);
  and and_10 (and10, in_1, in_2, not_26_out, in_4, not_27_out);

  // Other names for the same wires on the sheet: In1_t = in_4; In2_t = in_5; Q0_t = in_1; Q1_t = in_2; Q2_t = in_3
endmodule

module D2_logic (
  input  in_1,
  input  in_2,
  input  in_3,
  input  in_4,
  input  in_5,
  output D2
);

  wire and1, and2, and3, and4, and5, and6, and7, and8, and9, and10, not_1_out, not_2_out, not_3_out,
       not_4_out, not_5_out, not_6_out, not_7_out, not_8_out, not_9_out, not_10_out, not_11_out, not_12_out,
       not_13_out, not_14_out, not_15_out, not_16_out, not_17_out, not_18_out, not_19_out, not_20_out,
       not_21_out, not_22_out, not_23_out, not_24_out, not_25_out, not_26_out;

  not not_1 (not_1_out, in_1);
  not not_2 (not_2_out, in_2);
  not not_3 (not_3_out, in_3);
  not not_4 (not_4_out, in_4);
  not not_5 (not_5_out, in_1);
  not not_6 (not_6_out, in_2);
  not not_7 (not_7_out, in_4);
  not not_8 (not_8_out, in_5);
  not not_9 (not_9_out, in_1);
  not not_10 (not_10_out, in_2);
  not not_11 (not_11_out, in_4);
  and and_1 (and1, not_1_out, not_2_out, not_3_out, not_4_out, in_5);
  and and_2 (and2, not_5_out, not_6_out, in_3, not_7_out, not_8_out);
  and and_3 (and3, not_9_out, not_10_out, in_3, not_11_out, in_5);
  not not_12 (not_12_out, in_1);
  not not_13 (not_13_out, in_2);
  not not_14 (not_14_out, in_1);
  not not_15 (not_15_out, in_4);
  not not_16 (not_16_out, in_5);
  not not_17 (not_17_out, in_1);
  not not_18 (not_18_out, in_5);
  and and_4 (and4, not_12_out, not_13_out, in_3, in_4, in_5);
  and and_5 (and5, not_14_out, in_2, in_3, not_15_out, not_16_out);
  and and_6 (and6, not_17_out, in_2, in_3, in_4, not_18_out);
  not not_19 (not_19_out, in_1);
  not not_20 (not_20_out, in_2);
  not not_21 (not_21_out, in_4);
  not not_22 (not_22_out, in_5);
  not not_23 (not_23_out, in_2);
  not not_24 (not_24_out, in_4);
  and and_7 (and7, not_19_out, in_2, in_3, in_4, in_5);
  and and_8 (and8, in_1, not_20_out, in_3, not_21_out, not_22_out);
  and and_9 (and9, in_1, not_23_out, in_3, not_24_out, in_5);
  or or_1 (D2, and1, and2, and3, and4, and5, and6, and7, and8, and9, and10);
  not not_25 (not_25_out, in_2);
  not not_26 (not_26_out, in_5);
  and and_10 (and10, in_1, not_25_out, in_3, in_4, not_26_out);

  // Other names for the same wires on the sheet: In1_t = in_4; In2_t = in_5; Q0_t = in_1; Q1_t = in_2; Q2_t = in_3
endmodule

module DOH_logic (
  input  in_1,
  input  in_2,
  input  in_3,
  output DOH
);

  wire not_1_out;

  not not_1 (not_1_out, in_2);
  and and_1 (DOH, in_1, not_1_out, in_3);

  // Other names for the same wires on the sheet: Q0_t = in_1; Q1_t = in_2; Q2_t = in_3
endmodule

module DESPERATE_logic (
  input  in_1,
  input  in_2,
  input  in_3,
  output DESPERATE
);

  wire and1, and2, not_1_out, not_2_out;

  not not_1 (not_1_out, in_2);
  not not_2 (not_2_out, in_3);
  and and_1 (and1, in_1, not_1_out, in_3);
  and and_2 (and2, in_1, in_2, not_2_out);
  or or_1 (DESPERATE, and1, and2);

  // Other names for the same wires on the sheet: Q0_t = in_1; Q1_t = in_2; Q2_t = in_3
endmodule

module DISPENSE_logic (
  input  in_1,
  input  in_2,
  input  in_3,
  output out_4
);

  wire and1, and2, and3, not_1_out, not_2_out, not_3_out, not_4_out;

  not not_1 (not_1_out, in_2);
  not not_2 (not_2_out, in_3);
  not not_3 (not_3_out, in_2);
  not not_4 (not_4_out, in_3);
  and and_1 (and1, in_1, not_1_out, not_2_out);
  and and_2 (and2, in_1, not_3_out, in_3);
  and and_3 (and3, in_1, in_2, not_4_out);
  or or_1 (out_4, and1, and2, and3);

  // Other names for the same wires on the sheet: Q0_t = in_1; Q1_t = in_2; Q2_t = in_3
endmodule
