// Logisim project cpu.circ as structural Verilog: 15 circuits, main circuit main
module adder16 (
  input  [15:0] A,
  input  [15:0] B,
  input  sub,
  output [15:0] result,
  output ovf
);

  wire adder1_1_cout1, adder5_1_cout5, adder5_2_cout5, adder5_3_cout5, B_3;
  wire [4:0] B_0, B_1, B_2;

  adder5 adder5_1 (.Cin5(sub), .a5(A[4:0]), .b5(B_0), .sum5(result[4:0]), .Cout5(adder5_1_cout5));
  adder5 adder5_2 (.Cin5(adder5_1_cout5), .a5(A[9:5]), .b5(B_1), .sum5(result[9:5]), .Cout5(adder5_2_cout5));
  adder5 adder5_3 (.Cin5(adder5_2_cout5), .a5(A[14:10]), .b5(B_2), .sum5(result[14:10]), .Cout5(adder5_3_cout5));
  xor xor_1 (B_3, sub, B[15]);
  assign B_2 = {5{sub}} ^ B[14:10];  // XOR_Gate xor_2, 5 bits wide
  assign B_1 = {5{sub}} ^ B[9:5];  // XOR_Gate xor_3, 5 bits wide
  assign B_0 = {5{sub}} ^ B[4:0];  // XOR_Gate xor_4, 5 bits wide
  adder1 adder1_1 (.Cin1(adder5_3_cout5), .a1(A[15]), .b1(B_3), .sum1(result[15]), .Cout1(adder1_1_cout1));
  xor xor_5 (ovf, adder5_3_cout5, adder1_1_cout1);

  // Other names for the same wires on the sheet: sub_tun = sub; A_0[4:0] = A[4:0]; A_1[4:0] = A[9:5];
  //   A_2[4:0] = A[14:10]; A_3 = A[15]; B_0s[4:0] = B[4:0]; B_1s[4:0] = B[9:5]; B_2s[4:0] = B[14:10]; B_3s = B[15];
  //   result_0[4:0] = result[4:0]; result_1[4:0] = result[9:5]; result_2[4:0] = result[14:10]; result_3 = result[15]
endmodule

module single_register (
  input  [15:0] D,
  input  WE,
  input  clk,
  input  reset,
  output [15:0] Q
);

  wire clkt;

  and and_1 (clkt, WE, clk);
  D_Flip_Flop one (.D(D[0]), .clk(clkt), .Q(Q[0]), .reset(reset));  // open: Qn, preset
  D_Flip_Flop five (.D(D[4]), .clk(clkt), .Q(Q[4]), .reset(reset));  // open: Qn, preset
  D_Flip_Flop nine (.D(D[8]), .clk(clkt), .Q(Q[8]), .reset(reset));  // open: Qn, preset
  D_Flip_Flop thirteen (.D(D[12]), .clk(clkt), .Q(Q[12]), .reset(reset));  // open: Qn, preset
  D_Flip_Flop two (.D(D[1]), .clk(clkt), .Q(Q[1]), .reset(reset));  // open: Qn, preset
  D_Flip_Flop six (.D(D[5]), .clk(clkt), .Q(Q[5]), .reset(reset));  // open: Qn, preset
  D_Flip_Flop ten (.D(D[9]), .clk(clkt), .Q(Q[9]), .reset(reset));  // open: Qn, preset
  D_Flip_Flop fourteen (.D(D[13]), .clk(clkt), .Q(Q[13]), .reset(reset));  // open: Qn, preset
  D_Flip_Flop three (.D(D[2]), .clk(clkt), .Q(Q[2]), .reset(reset));  // open: Qn, preset
  D_Flip_Flop seven (.D(D[6]), .clk(clkt), .Q(Q[6]), .reset(reset));  // open: Qn, preset
  D_Flip_Flop eleven (.D(D[10]), .clk(clkt), .Q(Q[10]), .reset(reset));  // open: Qn, preset
  D_Flip_Flop fifteen (.D(D[14]), .clk(clkt), .Q(Q[14]), .reset(reset));  // open: Qn, preset
  D_Flip_Flop four (.D(D[3]), .clk(clkt), .Q(Q[3]), .reset(reset));  // open: Qn, preset
  D_Flip_Flop eight (.D(D[7]), .clk(clkt), .Q(Q[7]), .reset(reset));  // open: Qn, preset
  D_Flip_Flop twelve (.D(D[11]), .clk(clkt), .Q(Q[11]), .reset(reset));  // open: Qn, preset
  D_Flip_Flop sixteen (.D(D[15]), .clk(clkt), .Q(Q[15]), .reset(reset));  // open: Qn, preset

  // Other names for the same wires on the sheet: d1 = D[0]; d2 = D[1]; d3 = D[2]; d4 = D[3]; d5 = D[4]; d6 = D[5];
  //   d7 = D[6]; d8 = D[7]; d9 = D[8]; d10 = D[9]; d11 = D[10]; d12 = D[11]; d13 = D[12]; d14 = D[13]; d15 = D[14];
  //   d16 = D[15]; q1 = Q[0]; q2 = Q[1]; q3 = Q[2]; q4 = Q[3]; q5 = Q[4]; q6 = Q[5]; q7 = Q[6]; q8 = Q[7]; q9 = Q[8];
  //   q10 = Q[9]; q11 = Q[10]; q12 = Q[11]; q13 = Q[12]; q14 = Q[13]; q15 = Q[14]; q16 = Q[15]; resett = reset
endmodule

module RegisterFile (
  input  reset,
  input  [15:0] writeData,
  input  [2:0] rd,
  input  [2:0] rs,
  input  [2:0] rt,
  input  regWriteEnable,
  input  clk,
  output [15:0] rsVal,
  output [15:0] rtVal
);

  wire decoder_2_out0, decoder_2_out1, decoder_2_out2, decoder_2_out3, decoder_2_out4, decoder_2_out5,
       decoder_2_out6, decoder_2_out7, decoder_3_out0, decoder_3_out1, decoder_3_out2, decoder_3_out3,
       decoder_3_out4, decoder_3_out5, decoder_3_out6, decoder_3_out7, we0, we1, we2, we3, we4, we5, we6, we7;
  wire [15:0] q1, q2, q3, q4, q5, q6, q7;

  Decoder #(.select(3)) decoder_1 (
    .out0(we0), .out1(we1), .out2(we2), .out3(we3), .out4(we4), .out5(we5), .out6(we6), .out7(we7), .sel(rd),
    .en(regWriteEnable));
  // Probe on {16{1'b0}}
  // Probe on q1
  single_register single_register_1 (.Q(q1), .reset(reset), .clk(clk), .WE(we1), .D(writeData));
  // Probe on q2
  single_register single_register_2 (.Q(q2), .reset(reset), .clk(clk), .WE(we2), .D(writeData));
  // Probe on q3
  single_register single_register_3 (.Q(q3), .reset(reset), .clk(clk), .WE(we3), .D(writeData));
  // Probe on q4
  single_register single_register_4 (.Q(q4), .reset(reset), .clk(clk), .WE(we4), .D(writeData));
  // Probe on q5
  single_register single_register_5 (.Q(q5), .reset(reset), .clk(clk), .WE(we5), .D(writeData));
  // Probe on q6
  single_register single_register_6 (.Q(q6), .reset(reset), .clk(clk), .WE(we6), .D(writeData));
  // Probe on q7
  single_register single_register_7 (.Q(q7), .reset(reset), .clk(clk), .WE(we7), .D(writeData));
  assign rsVal = decoder_2_out0 ? {16{1'b0}} : 16'bz;  // Controlled_Buffer controlled_buffer_1
  Decoder #(.select(3)) decoder_2 (
    .out0(decoder_2_out0), .out1(decoder_2_out1), .out2(decoder_2_out2), .out3(decoder_2_out3),
    .out4(decoder_2_out4), .out5(decoder_2_out5), .out6(decoder_2_out6), .out7(decoder_2_out7), .sel(rs));  // open: en
  assign rtVal = decoder_3_out0 ? {16{1'b0}} : 16'bz;  // Controlled_Buffer controlled_buffer_2
  Decoder #(.select(3)) decoder_3 (
    .out0(decoder_3_out0), .out1(decoder_3_out1), .out2(decoder_3_out2), .out3(decoder_3_out3),
    .out4(decoder_3_out4), .out5(decoder_3_out5), .out6(decoder_3_out6), .out7(decoder_3_out7), .sel(rt));  // open: en
  assign rsVal = decoder_2_out1 ? q1 : 16'bz;  // Controlled_Buffer controlled_buffer_3
  assign rsVal = decoder_2_out2 ? q2 : 16'bz;  // Controlled_Buffer controlled_buffer_4
  assign rsVal = decoder_2_out3 ? q3 : 16'bz;  // Controlled_Buffer controlled_buffer_5
  assign rsVal = decoder_2_out4 ? q4 : 16'bz;  // Controlled_Buffer controlled_buffer_6
  assign rtVal = decoder_3_out1 ? q1 : 16'bz;  // Controlled_Buffer controlled_buffer_7
  assign rtVal = decoder_3_out2 ? q2 : 16'bz;  // Controlled_Buffer controlled_buffer_8
  assign rtVal = decoder_3_out3 ? q3 : 16'bz;  // Controlled_Buffer controlled_buffer_9
  assign rtVal = decoder_3_out4 ? q4 : 16'bz;  // Controlled_Buffer controlled_buffer_10
  assign rsVal = decoder_2_out5 ? q5 : 16'bz;  // Controlled_Buffer controlled_buffer_11
  assign rsVal = decoder_2_out6 ? q6 : 16'bz;  // Controlled_Buffer controlled_buffer_12
  assign rsVal = decoder_2_out7 ? q7 : 16'bz;  // Controlled_Buffer controlled_buffer_13
  assign rtVal = decoder_3_out5 ? q5 : 16'bz;  // Controlled_Buffer controlled_buffer_14
  assign rtVal = decoder_3_out6 ? q6 : 16'bz;  // Controlled_Buffer controlled_buffer_15
  assign rtVal = decoder_3_out7 ? q7 : 16'bz;  // Controlled_Buffer controlled_buffer_16

  // Other names for the same wires on the sheet: clkt = clk; rd1[15:0] = rsVal; rd2[15:0] = rtVal;
  //   readReg1t[2:0] = rs; readReg2t[2:0] = rt; regWriteEnablet = regWriteEnable; resett = reset;
  //   writeDatat[15:0] = writeData; writeRegt[2:0] = rd
endmodule

module adder1 (
  input  Cin1,
  input  a1,
  input  b1,
  output sum1,
  output Cout1
);

  wire and_1_out, and_2_out, xor_1_out;

  and and_1 (and_1_out, b1, a1);
  xor xor_1 (xor_1_out, a1, b1);
  or or_1 (Cout1, and_1_out, and_2_out);
  and and_2 (and_2_out, xor_1_out, Cin1);
  xor xor_2 (sum1, Cin1, xor_1_out);
endmodule

module adder5 (
  input  Cin5,
  input  [4:0] a5,
  input  [4:0] b5,
  output [4:0] sum5,
  output Cout5
);

  wire adder1_1_cout1, adder1_2_cout1, adder1_3_cout1, adder1_4_cout1;

  adder1 adder1_1 (.Cin1(Cin5), .a1(a5[0]), .b1(b5[0]), .sum1(sum5[0]), .Cout1(adder1_1_cout1));
  adder1 adder1_2 (.Cin1(adder1_1_cout1), .a1(a5[1]), .b1(b5[1]), .sum1(sum5[1]), .Cout1(adder1_2_cout1));
  adder1 adder1_3 (.Cin1(adder1_2_cout1), .a1(a5[2]), .b1(b5[2]), .sum1(sum5[2]), .Cout1(adder1_3_cout1));
  adder1 adder1_4 (.Cin1(adder1_3_cout1), .a1(a5[3]), .b1(b5[3]), .sum1(sum5[3]), .Cout1(adder1_4_cout1));
  adder1 adder1_5 (.Cin1(adder1_4_cout1), .a1(a5[4]), .b1(b5[4]), .sum1(sum5[4]), .Cout1(Cout5));

  // Other names for the same wires on the sheet: a5_0 = a5[0]; a5_1 = a5[1]; a5_2 = a5[2]; a5_3 = a5[3]; a5_4 = a5[4];
  //   b5_0 = b5[0]; b5_1 = b5[1]; b5_2 = b5[2]; b5_3 = b5[3]; b5_4 = b5[4]; sum5_0 = sum5[0]; sum5_1 = sum5[1];
  //   sum5_2 = sum5[2]; sum5_3 = sum5[3]; sum5_4 = sum5[4]
endmodule

module main (
  input  [2:0] rs,
  input  [2:0] rt,
  input  [2:0] rd,
  input  [5:0] Immediate,
  input  [2:0] ALUopp,
  input  reset,
  input  regFileWE,
  input  controlRtMUX,
  input  [2:0] Shamt,
  input  subract,
  input  bne,
  input  ble,
  input  jump,
  input  RAMWE,
  input  lwMUX,
  input  inputMUX,
  input  TTYWE,
  input  keyboardRE,
  input  rdstMUX,
  input  [11:0] address,
  input  jumpRegister
);

  wire ALUopp1, ALUopp2, ALUopp3, and_1_out, and_2_out, Available, ble_t, bne_t, clk, controlRtMUX_t,
       inputMUX_t, isNeg, isZero, jump_t, jumpRegister_t, keyboardRE_t, lwMUX_t, memory_latch_1_oe_latched,
       memory_latch_1_we_latched, not_1_out, not_2_out, not_3_out, or_1_out, or_2_out, RAMWE_t, rdstMUX_t,
       regFileWE_t, subtract, TTYWE_t;
  wire [2:0] multiplexer_1_out, rdst;
  wire [6:0] keyboardOutShort;
  wire [7:7] not_4_out;
  wire [11:0] address_t;
  wire [15:0] adder16_1_result, adder16_2_result, alu_1_outputdata, inputData2, keyboardOutput,
       memory_latch_1_address_latched, memory_latch_1_data_in_latched, multiplexer_4_out, multiplexer_7_out,
       multiplexer_8_out, multiplexer_9_out, multiplexer_10_out, pc_1_pcout, ram_1_dout, rsVal, rtVal,
       sign_extend_1_output1, sign_extend_2_output1, writeData;
  wire [15:12] rom_1_data;

  Clock clock_1 (.out(clk));
  not not_1 (not_1_out, clk);
  // Probe on pc_1_pcout
  PC pc_1 (.pcIn(multiplexer_8_out), .WE(1'b1), .clock(not_1_out), .reset(reset), .pcOut(pc_1_pcout));
  ROM #(.addrWidth(16), .dataWidth(16)) rom_1 (.addr(pc_1_pcout), .data({rom_1_data, address_t}));
  control_unit control_unit_1 (
    .opcode(rom_1_data), .ALUopp1(ALUopp1), .subtract(subtract), .ble(ble_t), .RAMWE(RAMWE_t),
    .TTYWE(TTYWE_t), .jumpRegister(jumpRegister_t), .controlRtMUX(controlRtMUX_t), .jump(jump_t),
    .lwMUX(lwMUX_t), .keyboardRE(keyboardRE_t), .ALUopp2(ALUopp2), .ALUopp3(ALUopp3), .bne(bne_t),
    .regFileWE(regFileWE_t), .inputMUX(inputMUX_t), .rdstMUX(rdstMUX_t));
  adder16 adder16_1 (.A(16'h1), .B(pc_1_pcout), .result(adder16_1_result));  // open: sub, ovf
  sign_extend sign_extend_1 (.Input1(address_t[5:0]), .Output1(sign_extend_1_output1));
  not not_2 (not_2_out, clk);
  // Probe on writeData
  Multiplexer #(.width(3), .enable("false")) multiplexer_1 (
    .in0(address_t[5:3]), .in1(address_t[8:6]), .out(multiplexer_1_out), .sel(rdstMUX_t));
  Keyboard keyboard_1 (.clk(not_2_out), .re(keyboardRE_t), .clr(reset), .avail(Available), .data(keyboardOutShort));
  Multiplexer #(.width(3), .enable("false")) multiplexer_2 (
    .in0(multiplexer_1_out), .in1(3'b111), .out(rdst), .sel(jump_t));
  Multiplexer #(.width(16), .enable("false")) multiplexer_3 (
    .in0(multiplexer_9_out), .in1(adder16_1_result), .out(writeData), .sel(jump_t));
  // Probe on keyboardOutShort
  adder16 adder16_2 (.A(sign_extend_1_output1), .B(adder16_1_result), .result(adder16_2_result));  // open: sub, ovf
  // Probe on rtVal
  // Probe on rsVal
  RegisterFile registerfile_1 (
    .reset(reset), .writeData(writeData), .rd(rdst), .rs(address_t[11:9]), .rt(address_t[8:6]),
    .regWriteEnable(regFileWE_t), .clk(clk), .rsVal(rsVal), .rtVal(rtVal));
  not not_3 (not_3_out, isZero);
  // Probe on rsVal
  not not_4 (not_4_out[7], Available);
  or or_1 (or_1_out, isNeg, isZero);
  and and_1 (and_1_out, or_1_out, ble_t);
  and and_2 (and_2_out, not_3_out, bne_t);
  Multiplexer #(.width(16), .enable("false")) multiplexer_4 (
    .in0(adder16_1_result), .in1(adder16_2_result), .out(multiplexer_4_out), .sel(or_2_out));
  or or_2 (or_2_out, and_1_out, and_2_out);
  sign_extend sign_extend_2 (.Input1(address_t[5:0]), .Output1(sign_extend_2_output1));
  TTY #(.rows(13), .cols(80)) tty_1 (.data(rsVal[6:0]), .clk(clk), .we(TTYWE_t), .clr(reset));
  // Probe on keyboardOutput
  Multiplexer #(.width(16), .enable("false")) multiplexer_5 (
    .in0({16{1'b0}}), .in1({{8{1'b0}}, not_4_out[7], keyboardOutShort}), .out(keyboardOutput), .sel(Available));
  Multiplexer #(.width(16), .enable("false")) multiplexer_6 (
    .in0(sign_extend_2_output1), .in1(rtVal), .out(inputData2), .sel(controlRtMUX_t));
  Multiplexer #(.width(16), .enable("false")) multiplexer_7 (
    .in0(multiplexer_4_out), .in1({multiplexer_4_out[15:12], address_t}), .out(multiplexer_7_out),
    .sel(jump_t));
  ALU alu_1 (
    .inputData1(rsVal), .inputData2(inputData2), .opType({ALUopp1, ALUopp2, ALUopp3}), .subtract(subtract),
    .shamt(address_t[2:0]), .outputData(alu_1_outputdata), .isZero(isZero), .isNeg(isNeg));
  Multiplexer #(.width(16), .enable("false")) multiplexer_8 (
    .in0(multiplexer_7_out), .in1(rsVal), .out(multiplexer_8_out), .sel(jumpRegister_t));
  Multiplexer #(.width(16), .enable("false")) multiplexer_9 (
    .in0(multiplexer_10_out), .in1(keyboardOutput), .out(multiplexer_9_out), .sel(inputMUX_t));
  RAM #(.addrWidth(16), .dataWidth(16), .trigger("high"), .databus("bibus")) ram_1 (
    .addr(memory_latch_1_address_latched), .we(memory_latch_1_we_latched), .oe(memory_latch_1_oe_latched),
    .din(memory_latch_1_data_in_latched), .dout(ram_1_dout));
  memory_latch memory_latch_1 (
    .OE_latched(memory_latch_1_oe_latched), .WE_latched(memory_latch_1_we_latched),
    .address_latched(memory_latch_1_address_latched), .data_in(rtVal), .clk(clk), .WE(RAMWE_t),
    .address(alu_1_outputdata), .data_in_latched(memory_latch_1_data_in_latched));
  Multiplexer #(.width(16), .enable("false")) multiplexer_10 (
    .in0(alu_1_outputdata), .in1(ram_1_dout), .out(multiplexer_10_out), .sel(lwMUX_t));

  // Other names for the same wires on the sheet: Immediate_t[5:0] = address_t[5:0]; Shamt_t[2:0] = address_t[2:0];
  //   Rd_t[2:0] = address_t[5:3]; Rt_t[2:0] = address_t[8:6]; Rs_t[2:0] = address_t[11:9];
  //   ALUopp_t[2:0] = {ALUopp1, ALUopp2, ALUopp3}

  // Notes on the sheet:
  //   contents of rom_1 (hex, n*v repeats v):
  //   104a e040 12a0 f400 e040 12a0 f400 e040 12a0 f400 a03f 8880 88c1 1080 10c0 7880 78c1 a03f
  //   Insn Memory
  //   Instruction types
  //   J
  //   I
  //   R
  //   keyboard
  //   branch mux
  //   choose rt or immediate
  //   output display
  //   jump mux
endmodule

module ALU (
  input  [15:0] inputData1,
  input  [15:0] inputData2,
  input  [2:0] opType,
  input  subtract,
  input  [2:0] shamt,
  output [15:0] outputData,
  output isZero,
  output isNeg
);

  wire or_2_out;
  wire [15:0] addOut, andOut, leftShiftOut, notOut, orOut, righShiftOut;

  assign andOut = inputData1 & inputData2;  // AND_Gate and_1, 16 bits wide
  assign orOut = inputData1 | inputData2;  // OR_Gate or_1, 16 bits wide
  assign notOut = ~inputData1;  // NOT_Gate not_1, 16 bits wide
  right_shift right_shift_1 (.shamt(shamt), .In1(inputData1), .Out1(righShiftOut));
  left_shift left_shift_1 (.shamt(shamt), .In1(inputData1), .Out1(leftShiftOut));
  adder16 adder16_1 (.A(inputData1), .B(inputData2), .sub(subtract), .result(addOut));  // open: ovf
  Multiplexer #(.select(3), .width(16), .enable("false")) multiplexer_1 (
    .in0(righShiftOut), .in1(leftShiftOut), .in2(addOut), .in3(andOut), .in4(orOut), .in5(notOut),
    .out({isNeg, outputData[14:0]}), .sel(opType));  // open: in6, in7
  or or_2 (or_2_out, outputData[0], outputData[1], outputData[2], outputData[3], outputData[4], outputData[5], outputData[6], outputData[7], outputData[8], outputData[9], outputData[10], outputData[11], outputData[12], outputData[13], outputData[14], isNeg);
  not not_2 (isZero, or_2_out);

  assign outputData[15] = isNeg;

  // Other names for the same wires on the sheet: check[15:0] = {isNeg, outputData[14:0]}; In1[15:0] = inputData1;
  //   In2[15:0] = inputData2

  // Notes on the sheet:
  //   000-rightshift, 001-leftshift, 010-add, 011-and, 100-or, 101-not
endmodule

module left_shift (
  input  [2:0] shamt,
  input  [15:0] In1,
  output [15:0] Out1
);

  wire multiplexer_1_out, multiplexer_2_out, multiplexer_3_out, multiplexer_4_out, multiplexer_5_out,
       multiplexer_6_out, multiplexer_7_out, multiplexer_8_out, multiplexer_9_out, multiplexer_10_out,
       multiplexer_11_out, multiplexer_12_out, multiplexer_13_out, multiplexer_14_out, multiplexer_15_out,
       multiplexer_16_out, multiplexer_17_out, multiplexer_18_out, multiplexer_19_out, multiplexer_20_out,
       multiplexer_21_out, multiplexer_22_out, multiplexer_23_out, multiplexer_24_out, multiplexer_25_out,
       multiplexer_26_out, multiplexer_27_out, multiplexer_28_out, multiplexer_29_out, multiplexer_30_out,
       multiplexer_31_out, multiplexer_32_out;

  Multiplexer #(.enable("false")) multiplexer_1 (.in0(In1[15]), .in1(In1[11]), .out(multiplexer_1_out), .sel(shamt[2]));
  Multiplexer #(.enable("false")) multiplexer_2 (.in0(In1[14]), .in1(In1[10]), .out(multiplexer_2_out), .sel(shamt[2]));
  Multiplexer #(.enable("false")) multiplexer_3 (.in0(In1[13]), .in1(In1[9]), .out(multiplexer_3_out), .sel(shamt[2]));
  Multiplexer #(.enable("false")) multiplexer_4 (.in0(In1[12]), .in1(In1[8]), .out(multiplexer_4_out), .sel(shamt[2]));
  Multiplexer #(.enable("false")) multiplexer_5 (.in0(In1[11]), .in1(In1[7]), .out(multiplexer_5_out), .sel(shamt[2]));
  Multiplexer #(.enable("false")) multiplexer_6 (.in0(In1[10]), .in1(In1[6]), .out(multiplexer_6_out), .sel(shamt[2]));
  Multiplexer #(.enable("false")) multiplexer_7 (.in0(In1[9]), .in1(In1[5]), .out(multiplexer_7_out), .sel(shamt[2]));
  Multiplexer #(.enable("false")) multiplexer_8 (.in0(In1[8]), .in1(In1[4]), .out(multiplexer_8_out), .sel(shamt[2]));
  Multiplexer #(.enable("false")) multiplexer_9 (.in0(In1[7]), .in1(In1[3]), .out(multiplexer_9_out), .sel(shamt[2]));
  Multiplexer #(.enable("false")) multiplexer_10 (.in0(In1[6]), .in1(In1[2]), .out(multiplexer_10_out), .sel(shamt[2]));
  Multiplexer #(.enable("false")) multiplexer_11 (.in0(In1[5]), .in1(In1[1]), .out(multiplexer_11_out), .sel(shamt[2]));
  Multiplexer #(.enable("false")) multiplexer_12 (.in0(In1[4]), .in1(In1[0]), .out(multiplexer_12_out), .sel(shamt[2]));
  Multiplexer #(.enable("false")) multiplexer_13 (.in0(In1[3]), .in1(1'b0), .out(multiplexer_13_out), .sel(shamt[2]));
  Multiplexer #(.enable("false")) multiplexer_14 (.in0(In1[2]), .in1(1'b0), .out(multiplexer_14_out), .sel(shamt[2]));
  Multiplexer #(.enable("false")) multiplexer_15 (.in0(In1[1]), .in1(1'b0), .out(multiplexer_15_out), .sel(shamt[2]));
  Multiplexer #(.enable("false")) multiplexer_16 (.in0(In1[0]), .in1(1'b0), .out(multiplexer_16_out), .sel(shamt[2]));
  Multiplexer #(.enable("false")) multiplexer_17 (
    .in0(multiplexer_1_out), .in1(multiplexer_3_out), .out(multiplexer_17_out), .sel(shamt[1]));
  Multiplexer #(.enable("false")) multiplexer_18 (
    .in0(multiplexer_2_out), .in1(multiplexer_4_out), .out(multiplexer_18_out), .sel(shamt[1]));
  Multiplexer #(.enable("false")) multiplexer_19 (
    .in0(multiplexer_3_out), .in1(multiplexer_5_out), .out(multiplexer_19_out), .sel(shamt[1]));
  Multiplexer #(.enable("false")) multiplexer_20 (
    .in0(multiplexer_4_out), .in1(multiplexer_6_out), .out(multiplexer_20_out), .sel(shamt[1]));
  Multiplexer #(.enable("false")) multiplexer_21 (
    .in0(multiplexer_5_out), .in1(multiplexer_7_out), .out(multiplexer_21_out), .sel(shamt[1]));
  Multiplexer #(.enable("false")) multiplexer_22 (
    .in0(multiplexer_6_out), .in1(multiplexer_8_out), .out(multiplexer_22_out), .sel(shamt[1]));
  Multiplexer #(.enable("false")) multiplexer_23 (
    .in0(multiplexer_7_out), .in1(multiplexer_9_out), .out(multiplexer_23_out), .sel(shamt[1]));
  Multiplexer #(.enable("false")) multiplexer_24 (
    .in0(multiplexer_8_out), .in1(multiplexer_10_out), .out(multiplexer_24_out), .sel(shamt[1]));
  Multiplexer #(.enable("false")) multiplexer_25 (
    .in0(multiplexer_9_out), .in1(multiplexer_11_out), .out(multiplexer_25_out), .sel(shamt[1]));
  Multiplexer #(.enable("false")) multiplexer_26 (
    .in0(multiplexer_10_out), .in1(multiplexer_12_out), .out(multiplexer_26_out), .sel(shamt[1]));
  Multiplexer #(.enable("false")) multiplexer_27 (
    .in0(multiplexer_11_out), .in1(multiplexer_13_out), .out(multiplexer_27_out), .sel(shamt[1]));
  Multiplexer #(.enable("false")) multiplexer_28 (
    .in0(multiplexer_12_out), .in1(multiplexer_14_out), .out(multiplexer_28_out), .sel(shamt[1]));
  Multiplexer #(.enable("false")) multiplexer_29 (
    .in0(multiplexer_13_out), .in1(multiplexer_15_out), .out(multiplexer_29_out), .sel(shamt[1]));
  Multiplexer #(.enable("false")) multiplexer_30 (
    .in0(multiplexer_14_out), .in1(multiplexer_16_out), .out(multiplexer_30_out), .sel(shamt[1]));
  Multiplexer #(.enable("false")) multiplexer_31 (
    .in0(multiplexer_15_out), .in1(1'b0), .out(multiplexer_31_out), .sel(shamt[1]));
  Multiplexer #(.enable("false")) multiplexer_32 (
    .in0(multiplexer_16_out), .in1(1'b0), .out(multiplexer_32_out), .sel(shamt[1]));
  Multiplexer #(.enable("false")) multiplexer_33 (
    .in0(multiplexer_17_out), .in1(multiplexer_18_out), .out(Out1[15]), .sel(shamt[0]));
  Multiplexer #(.enable("false")) multiplexer_34 (
    .in0(multiplexer_18_out), .in1(multiplexer_19_out), .out(Out1[14]), .sel(shamt[0]));
  Multiplexer #(.enable("false")) multiplexer_35 (
    .in0(multiplexer_19_out), .in1(multiplexer_20_out), .out(Out1[13]), .sel(shamt[0]));
  Multiplexer #(.enable("false")) multiplexer_36 (
    .in0(multiplexer_20_out), .in1(multiplexer_21_out), .out(Out1[12]), .sel(shamt[0]));
  Multiplexer #(.enable("false")) multiplexer_37 (
    .in0(multiplexer_21_out), .in1(multiplexer_22_out), .out(Out1[11]), .sel(shamt[0]));
  Multiplexer #(.enable("false")) multiplexer_38 (
    .in0(multiplexer_22_out), .in1(multiplexer_23_out), .out(Out1[10]), .sel(shamt[0]));
  Multiplexer #(.enable("false")) multiplexer_39 (
    .in0(multiplexer_23_out), .in1(multiplexer_24_out), .out(Out1[9]), .sel(shamt[0]));
  Multiplexer #(.enable("false")) multiplexer_40 (
    .in0(multiplexer_24_out), .in1(multiplexer_25_out), .out(Out1[8]), .sel(shamt[0]));
  Multiplexer #(.enable("false")) multiplexer_41 (
    .in0(multiplexer_25_out), .in1(multiplexer_26_out), .out(Out1[7]), .sel(shamt[0]));
  Multiplexer #(.enable("false")) multiplexer_42 (
    .in0(multiplexer_26_out), .in1(multiplexer_27_out), .out(Out1[6]), .sel(shamt[0]));
  Multiplexer #(.enable("false")) multiplexer_43 (
    .in0(multiplexer_27_out), .in1(multiplexer_28_out), .out(Out1[5]), .sel(shamt[0]));
  Multiplexer #(.enable("false")) multiplexer_44 (
    .in0(multiplexer_28_out), .in1(multiplexer_29_out), .out(Out1[4]), .sel(shamt[0]));
  Multiplexer #(.enable("false")) multiplexer_45 (
    .in0(multiplexer_29_out), .in1(multiplexer_30_out), .out(Out1[3]), .sel(shamt[0]));
  Multiplexer #(.enable("false")) multiplexer_46 (
    .in0(multiplexer_30_out), .in1(multiplexer_31_out), .out(Out1[2]), .sel(shamt[0]));
  Multiplexer #(.enable("false")) multiplexer_47 (
    .in0(multiplexer_31_out), .in1(multiplexer_32_out), .out(Out1[1]), .sel(shamt[0]));
  Multiplexer #(.enable("false")) multiplexer_48 (.in0(multiplexer_32_out), .in1(1'b0), .out(Out1[0]), .sel(shamt[0]));

  // Other names for the same wires on the sheet: b0 = In1[0]; b1 = In1[1]; b2 = In1[2]; b3 = In1[3]; b4 = In1[4];
  //   b5 = In1[5]; b6 = In1[6]; b7 = In1[7]; b8 = In1[8]; b9 = In1[9]; b10 = In1[10]; b11 = In1[11]; b12 = In1[12];
  //   b13 = In1[13]; b14 = In1[14]; b15 = In1[15]; outBit0 = Out1[0]; outBit1 = Out1[1]; outBit2 = Out1[2];
  //   outBit3 = Out1[3]; outBit4 = Out1[4]; outBit5 = Out1[5]; outBit6 = Out1[6]; outBit7 = Out1[7];
  //   outBit8 = Out1[8]; outBit9 = Out1[9]; outBit10 = Out1[10]; outBit11 = Out1[11]; outBit12 = Out1[12];
  //   outBit13 = Out1[13]; outBit14 = Out1[14]; outBit15 = Out1[15]; s2 = shamt[0]; s1 = shamt[1]; s0 = shamt[2]
endmodule

module right_shift (
  input  [2:0] shamt,
  input  [15:0] In1,
  output [15:0] Out1
);

  wire multiplexer_1_out, multiplexer_2_out, multiplexer_3_out, multiplexer_4_out, multiplexer_5_out,
       multiplexer_6_out, multiplexer_7_out, multiplexer_8_out, multiplexer_9_out, multiplexer_10_out,
       multiplexer_11_out, multiplexer_12_out, multiplexer_13_out, multiplexer_14_out, multiplexer_15_out,
       multiplexer_16_out, multiplexer_17_out, multiplexer_18_out, multiplexer_19_out, multiplexer_20_out,
       multiplexer_21_out, multiplexer_22_out, multiplexer_23_out, multiplexer_24_out, multiplexer_25_out,
       multiplexer_26_out, multiplexer_27_out, multiplexer_28_out, multiplexer_29_out, multiplexer_30_out,
       multiplexer_31_out, multiplexer_32_out;

  Multiplexer #(.enable("false")) multiplexer_1 (.in0(In1[0]), .in1(In1[4]), .out(multiplexer_1_out), .sel(shamt[2]));
  Multiplexer #(.enable("false")) multiplexer_2 (.in0(In1[1]), .in1(In1[5]), .out(multiplexer_2_out), .sel(shamt[2]));
  Multiplexer #(.enable("false")) multiplexer_3 (.in0(In1[2]), .in1(In1[6]), .out(multiplexer_3_out), .sel(shamt[2]));
  Multiplexer #(.enable("false")) multiplexer_4 (.in0(In1[3]), .in1(In1[7]), .out(multiplexer_4_out), .sel(shamt[2]));
  Multiplexer #(.enable("false")) multiplexer_5 (.in0(In1[4]), .in1(In1[8]), .out(multiplexer_5_out), .sel(shamt[2]));
  Multiplexer #(.enable("false")) multiplexer_6 (.in0(In1[5]), .in1(In1[9]), .out(multiplexer_6_out), .sel(shamt[2]));
  Multiplexer #(.enable("false")) multiplexer_7 (.in0(In1[6]), .in1(In1[10]), .out(multiplexer_7_out), .sel(shamt[2]));
  Multiplexer #(.enable("false")) multiplexer_8 (.in0(In1[7]), .in1(In1[11]), .out(multiplexer_8_out), .sel(shamt[2]));
  Multiplexer #(.enable("false")) multiplexer_9 (.in0(In1[8]), .in1(In1[12]), .out(multiplexer_9_out), .sel(shamt[2]));
  Multiplexer #(.enable("false")) multiplexer_10 (
    .in0(In1[9]), .in1(In1[13]), .out(multiplexer_10_out), .sel(shamt[2]));
  Multiplexer #(.enable("false")) multiplexer_11 (
    .in0(In1[10]), .in1(In1[14]), .out(multiplexer_11_out), .sel(shamt[2]));
  Multiplexer #(.enable("false")) multiplexer_12 (
    .in0(In1[11]), .in1(In1[15]), .out(multiplexer_12_out), .sel(shamt[2]));
  Multiplexer #(.enable("false")) multiplexer_13 (.in0(In1[12]), .in1(1'b0), .out(multiplexer_13_out), .sel(shamt[2]));
  Multiplexer #(.enable("false")) multiplexer_14 (.in0(In1[13]), .in1(1'b0), .out(multiplexer_14_out), .sel(shamt[2]));
  Multiplexer #(.enable("false")) multiplexer_15 (.in0(In1[14]), .in1(1'b0), .out(multiplexer_15_out), .sel(shamt[2]));
  Multiplexer #(.enable("false")) multiplexer_16 (.in0(In1[15]), .in1(1'b0), .out(multiplexer_16_out), .sel(shamt[2]));
  Multiplexer #(.enable("false")) multiplexer_17 (
    .in0(multiplexer_1_out), .in1(multiplexer_3_out), .out(multiplexer_17_out), .sel(shamt[1]));
  Multiplexer #(.enable("false")) multiplexer_18 (
    .in0(multiplexer_2_out), .in1(multiplexer_4_out), .out(multiplexer_18_out), .sel(shamt[1]));
  Multiplexer #(.enable("false")) multiplexer_19 (
    .in0(multiplexer_3_out), .in1(multiplexer_5_out), .out(multiplexer_19_out), .sel(shamt[1]));
  Multiplexer #(.enable("false")) multiplexer_20 (
    .in0(multiplexer_4_out), .in1(multiplexer_6_out), .out(multiplexer_20_out), .sel(shamt[1]));
  Multiplexer #(.enable("false")) multiplexer_21 (
    .in0(multiplexer_5_out), .in1(multiplexer_7_out), .out(multiplexer_21_out), .sel(shamt[1]));
  Multiplexer #(.enable("false")) multiplexer_22 (
    .in0(multiplexer_6_out), .in1(multiplexer_8_out), .out(multiplexer_22_out), .sel(shamt[1]));
  Multiplexer #(.enable("false")) multiplexer_23 (
    .in0(multiplexer_7_out), .in1(multiplexer_9_out), .out(multiplexer_23_out), .sel(shamt[1]));
  Multiplexer #(.enable("false")) multiplexer_24 (
    .in0(multiplexer_8_out), .in1(multiplexer_10_out), .out(multiplexer_24_out), .sel(shamt[1]));
  Multiplexer #(.enable("false")) multiplexer_25 (
    .in0(multiplexer_9_out), .in1(multiplexer_11_out), .out(multiplexer_25_out), .sel(shamt[1]));
  Multiplexer #(.enable("false")) multiplexer_26 (
    .in0(multiplexer_10_out), .in1(multiplexer_12_out), .out(multiplexer_26_out), .sel(shamt[1]));
  Multiplexer #(.enable("false")) multiplexer_27 (
    .in0(multiplexer_11_out), .in1(multiplexer_13_out), .out(multiplexer_27_out), .sel(shamt[1]));
  Multiplexer #(.enable("false")) multiplexer_28 (
    .in0(multiplexer_12_out), .in1(multiplexer_14_out), .out(multiplexer_28_out), .sel(shamt[1]));
  Multiplexer #(.enable("false")) multiplexer_29 (
    .in0(multiplexer_13_out), .in1(multiplexer_15_out), .out(multiplexer_29_out), .sel(shamt[1]));
  Multiplexer #(.enable("false")) multiplexer_30 (
    .in0(multiplexer_14_out), .in1(multiplexer_16_out), .out(multiplexer_30_out), .sel(shamt[1]));
  Multiplexer #(.enable("false")) multiplexer_31 (
    .in0(multiplexer_15_out), .in1(1'b0), .out(multiplexer_31_out), .sel(shamt[1]));
  Multiplexer #(.enable("false")) multiplexer_32 (
    .in0(multiplexer_16_out), .in1(1'b0), .out(multiplexer_32_out), .sel(shamt[1]));
  Multiplexer #(.enable("false")) multiplexer_33 (
    .in0(multiplexer_17_out), .in1(multiplexer_18_out), .out(Out1[0]), .sel(shamt[0]));
  Multiplexer #(.enable("false")) multiplexer_34 (
    .in0(multiplexer_18_out), .in1(multiplexer_19_out), .out(Out1[1]), .sel(shamt[0]));
  Multiplexer #(.enable("false")) multiplexer_35 (
    .in0(multiplexer_19_out), .in1(multiplexer_20_out), .out(Out1[2]), .sel(shamt[0]));
  Multiplexer #(.enable("false")) multiplexer_36 (
    .in0(multiplexer_20_out), .in1(multiplexer_21_out), .out(Out1[3]), .sel(shamt[0]));
  Multiplexer #(.enable("false")) multiplexer_37 (
    .in0(multiplexer_21_out), .in1(multiplexer_22_out), .out(Out1[4]), .sel(shamt[0]));
  Multiplexer #(.enable("false")) multiplexer_38 (
    .in0(multiplexer_22_out), .in1(multiplexer_23_out), .out(Out1[5]), .sel(shamt[0]));
  Multiplexer #(.enable("false")) multiplexer_39 (
    .in0(multiplexer_23_out), .in1(multiplexer_24_out), .out(Out1[6]), .sel(shamt[0]));
  Multiplexer #(.enable("false")) multiplexer_40 (
    .in0(multiplexer_24_out), .in1(multiplexer_25_out), .out(Out1[7]), .sel(shamt[0]));
  Multiplexer #(.enable("false")) multiplexer_41 (
    .in0(multiplexer_25_out), .in1(multiplexer_26_out), .out(Out1[8]), .sel(shamt[0]));
  Multiplexer #(.enable("false")) multiplexer_42 (
    .in0(multiplexer_26_out), .in1(multiplexer_27_out), .out(Out1[9]), .sel(shamt[0]));
  Multiplexer #(.enable("false")) multiplexer_43 (
    .in0(multiplexer_27_out), .in1(multiplexer_28_out), .out(Out1[10]), .sel(shamt[0]));
  Multiplexer #(.enable("false")) multiplexer_44 (
    .in0(multiplexer_28_out), .in1(multiplexer_29_out), .out(Out1[11]), .sel(shamt[0]));
  Multiplexer #(.enable("false")) multiplexer_45 (
    .in0(multiplexer_29_out), .in1(multiplexer_30_out), .out(Out1[12]), .sel(shamt[0]));
  Multiplexer #(.enable("false")) multiplexer_46 (
    .in0(multiplexer_30_out), .in1(multiplexer_31_out), .out(Out1[13]), .sel(shamt[0]));
  Multiplexer #(.enable("false")) multiplexer_47 (
    .in0(multiplexer_31_out), .in1(multiplexer_32_out), .out(Out1[14]), .sel(shamt[0]));
  Multiplexer #(.enable("false")) multiplexer_48 (.in0(multiplexer_32_out), .in1(1'b0), .out(Out1[15]), .sel(shamt[0]));

  // Other names for the same wires on the sheet: b0 = In1[0]; b1 = In1[1]; b2 = In1[2]; b3 = In1[3]; b4 = In1[4];
  //   b5 = In1[5]; b6 = In1[6]; b7 = In1[7]; b8 = In1[8]; b9 = In1[9]; b10 = In1[10]; b11 = In1[11]; b12 = In1[12];
  //   b13 = In1[13]; b14 = In1[14]; b15 = In1[15]; outBit0 = Out1[0]; outBit1 = Out1[1]; outBit2 = Out1[2];
  //   outBit3 = Out1[3]; outBit4 = Out1[4]; outBit5 = Out1[5]; outBit6 = Out1[6]; outBit7 = Out1[7];
  //   outBit8 = Out1[8]; outBit9 = Out1[9]; outBit10 = Out1[10]; outBit11 = Out1[11]; outBit12 = Out1[12];
  //   outBit13 = Out1[13]; outBit14 = Out1[14]; outBit15 = Out1[15]; s2 = shamt[0]; s1 = shamt[1]; s0 = shamt[2]
endmodule

module memory_latch (
  input  [15:0] address,
  input  WE,
  input  clk,
  input  [15:0] data_in,
  output [15:0] address_latched,
  output WE_latched,
  output OE_latched,
  output [15:0] data_in_latched
);

  wire DMwe_latch_q;
  wire [15:0] addr_latch_q;

  Register #(.width(16), .trigger("falling")) addr_latch (
    .D(address), .en(WE), .clk(clk), .Q(addr_latch_q));  // open: clr
  D_Flip_Flop #(.trigger("falling")) DMwe_latch (.D(WE), .clk(clk), .Q(DMwe_latch_q));  // open: Qn, preset, reset
  Register #(.width(16), .trigger("falling")) data_to_be_written (
    .D(data_in), .en(WE), .clk(clk), .Q(data_in_latched));  // open: clr
  Multiplexer #(.width(16), .enable("false")) multiplexer_1 (
    .in0(address), .in1(addr_latch_q), .out(address_latched), .sel(DMwe_latch_q));
  and and_1 (WE_latched, clk, DMwe_latch_q);
  not not_1 (OE_latched, WE_latched);
endmodule

module zero_extend (
  input  [5:0] Input1,
  output [15:0] Output1
);


  assign Output1 = {{10{1'b0}}, Input1};
endmodule

module one_extend (
  input  [5:0] Input1,
  output [15:0] Output1
);


  assign Output1 = {{10{1'b1}}, Input1};
endmodule

module sign_extend (
  input  [5:0] Input1,
  output [15:0] Output1
);

  wire [15:0] one_extend_1_output1, zero_extend_1_output1;

  zero_extend zero_extend_1 (.Input1(Input1), .Output1(zero_extend_1_output1));
  one_extend one_extend_1 (.Input1(Input1), .Output1(one_extend_1_output1));
  Multiplexer #(.width(16), .enable("false")) multiplexer_1 (
    .in0(zero_extend_1_output1), .in1(one_extend_1_output1), .out(Output1), .sel(Input1[5]));

  // Other names for the same wires on the sheet: bit0_4[4:0] = Input1[4:0]; data[5:0] = Input1; bit5 = Input1[5]
endmodule

module PC (
  input  [15:0] pcIn,
  input  WE,
  input  clock,
  input  reset,
  output [15:0] pcOut
);

  single_register PC (.Q(pcOut), .reset(reset), .clk(clock), .WE(WE), .D(pcIn));
endmodule

module control_unit (
  input  [3:0] opcode,
  output ALUopp1,
  output subtract,
  output ble,
  output RAMWE,
  output TTYWE,
  output jumpRegister,
  output controlRtMUX,
  output jump,
  output lwMUX,
  output keyboardRE,
  output ALUopp2,
  output ALUopp3,
  output bne,
  output regFileWE,
  output inputMUX,
  output rdstMUX
);

  wire add, addi, and1, j, jal, sll1, srl1, sub;

  Decoder #(.select(4)) decoder_1 (
    .out0(add), .out1(addi), .out2(sub), .out3(sll1), .out4(srl1), .out5(and1), .out6(ALUopp1), .out7(lwMUX),
    .out8(RAMWE), .out9(bne), .out10(ble), .out11(j), .out12(jumpRegister), .out13(jal), .out14(inputMUX),
    .out15(TTYWE), .sel(opcode));  // open: en
  or or_1 (ALUopp2, lwMUX, add, addi, sub, and1, bne, ble, RAMWE);
  or or_2 (ALUopp3, sll1, and1, ALUopp1);
  or or_3 (subtract, sub, bne, ble);
  or or_4 (controlRtMUX, add, sub, sll1, inputMUX, srl1, and1, bne, ble);
  or or_5 (jump, j, jal);
  or or_6 (regFileWE, inputMUX, add, addi, sub, sll1, and1, ALUopp1, lwMUX, jal, srl1);
  or or_7 (rdstMUX, addi, inputMUX, lwMUX);

  assign keyboardRE = inputMUX;

  // Other names for the same wires on the sheet: input1 = inputMUX; jr = jumpRegister; lw = lwMUX; not1 = ALUopp1;
  //   output1 = TTYWE; sw = RAMWE
endmodule
